# Fritzing sketch Acrobot_schematic (saved by Fritzing 0.9.3b)

parts:
  Part1 = Arduino Uno (Rev3)
  Part2 = Arduino Uno (Rev3)
  Yumo-enc1 = YumoE6B2
  Power_plug1 = Power plug
  J4 = Basic Servo
  Power_plug2 = Power plug  # not connected
  Power_plug3 = Power plug  # not connected
  Part3 = Arduino Uno (Rev3)
  Power_plug4 = Power plug  # not connected

nets:
  GND: Part1.GND, Part2.GND, Yumo-enc1.GND, Part3.GND
  N1: Part1.D0/RX, Part3.D2
  N2: Part1.D1/TX, Part3.D3_PWM
  N3: Part1.D3_PWM, J4.pulse
  N4: Part2.A4/SDA, Part3.A4/SDA
  N5: Part2.A5/SCL, Part3.A5/SCL
  N6: Part2.D2, Yumo-enc1.A
  N7: Part2.D3_PWM, Yumo-enc1.B
  N8: Part2.5V, Yumo-enc1.V
  GND_2: Power_plug1.GND, J4.gnd
  VCC: Power_plug1.VCC, J4.vcc

notes:
  +5V - 1A
  GND
  +9V - 1A
  Rotary Encoder

custom parts:
  YumoE6B2: Yumo E6B2-C incremental encoder. Resolutions 10 to 4000 pulses per revolution (depending on model number). Power from 5 to 24V (again depending on model). Dia 40mm body 30mm plus 20mm shaft.
